// Logisim project LC3-2200a.circ as structural Verilog: 5 circuits, main circuit Datapath
module Datapath (
);

  wire Clear, Clock, Dr__ALU, Dr__MEM, Dr__OFF, Dr__PC, Dr__REG, Ld_A, Ld_B, Ld_CC, Ld_IR, Ld_MAR, Ld_PC,
       not_1_out, Wr_MEM, Wr_REG;
  wire [1:0] CheckCC_out_3, func, micro_sequencer_1_out_6;
  wire [2:0] CC, comparator_1_gt;
  wire [3:0] regno;
  wire [23:0] bit_extender_1_out;
  wire [31:0] alu_1_output, bit_extender_2_out, controlled_buffer_1_out, IR, ram_1_data, regfile_1_out_6,
       register_1_q, register_2_q, register_3_q, register_4_q;

  Register #(.width(32)) register_1 (
    .D(controlled_buffer_1_out), .en(Ld_PC), .Q(register_1_q), .clk(Clock), .clr(Clear));
  assign controlled_buffer_1_out = Dr__PC ? register_1_q : 32'bz;  // Controlled_Buffer controlled_buffer_1
  Comparator #(.width(32), .mode("unsigned")) comparator_1 (
    .a(controlled_buffer_1_out), .b({32{1'b0}}), .gt(comparator_1_gt[0]), .eq(comparator_1_gt[1]),
    .lt(comparator_1_gt[2]));
  Register #(.width(32)) register_2 (
    .D(controlled_buffer_1_out), .en(Ld_A), .Q(register_2_q), .clk(Clock), .clr(Clear));
  Register #(.width(3)) u_CC (.D(comparator_1_gt), .en(Ld_CC), .Q(CC), .clk(Clock), .clr(Clear));
  Register #(.width(32)) register_3 (
    .D(controlled_buffer_1_out), .en(Ld_B), .Q(register_3_q), .clk(Clock), .clr(Clear));
  ALU alu_1 (.in_1(register_2_q), .in_2(register_3_q), .\output (alu_1_output), .in_3(func));
  assign controlled_buffer_1_out = Dr__ALU ? alu_1_output : 32'bz;  // Controlled_Buffer controlled_buffer_2
  checkCC CheckCC (.in_1(CC), .in_2(IR[22:20]), .out_3(CheckCC_out_3));
  Micro_sequencer micro_sequencer_1 (
    .in_1(IR[31:28]), .in_2(CheckCC_out_3), .out_5({Wr_MEM, Wr_REG}),
    .out_4({Ld_CC, Ld_B, Ld_A, Ld_MAR, Ld_IR, Ld_PC}), .out_3({Dr__OFF, Dr__PC, Dr__ALU, Dr__MEM, Dr__REG}),
    .out_6(micro_sequencer_1_out_6), .out_7(func));
  Clock clock_1 (.out(Clock));
  Button button_1 (.out(Clear));
  regFile regfile_1 (
    .in_1(Clock), .in_2(controlled_buffer_1_out), .in_3(Wr_REG), .in_4(Clear), .in_5(regno),
    .out_6(regfile_1_out_6));
  assign controlled_buffer_1_out = Dr__REG ? regfile_1_out_6 : 32'bz;  // Controlled_Buffer controlled_buffer_3
  Register #(.width(32)) register_4 (
    .D(controlled_buffer_1_out), .en(Ld_MAR), .Q(register_4_q), .clk(Clock), .clr(Clear));
  Bit_Extender #(.in_width(32), .out_width(24), .\type ("sign")) bit_extender_1 (
    .in(register_4_q), .out(bit_extender_1_out));
  Multiplexer #(.select(2), .width(4), .disabled(0), .enable("false")) multiplexer_1 (
    .in0(IR[27:24]), .in1(IR[23:20]), .in2(IR[3:0]), .out(regno), .sel(micro_sequencer_1_out_6));  // open: in3
  not not_1 (not_1_out, Wr_MEM);
  RAM #(.addrWidth(24), .dataWidth(32), .bus("separate")) ram_1 (
    .addr(bit_extender_1_out), .din(controlled_buffer_1_out), .data(ram_1_data), .str(Wr_MEM), .clk(Clock),
    .ld(not_1_out), .clr(Clear));  // open: sel
  assign controlled_buffer_1_out = Dr__MEM ? ram_1_data : 32'bz;  // Controlled_Buffer controlled_buffer_4
  Register #(.width(32)) register_5 (.D(controlled_buffer_1_out), .en(Ld_IR), .Q(IR), .clk(Clock), .clr(Clear));
  assign bit_extender_2_out = {{12{IR[19]}}, IR[19:0]};  // Bit_Extender bit_extender_2
  assign controlled_buffer_1_out = Dr__OFF ? bit_extender_2_out : 32'bz;  // Controlled_Buffer controlled_buffer_5

  // Other names for the same wires on the sheet: RZ[3:0] = IR[3:0]; ShfD = IR[18]; ShfA = IR[19]; RY[3:0] = IR[23:20];
  //   RX[3:0] = IR[27:24]; OP[3:0] = IR[31:28]

  // Notes on the sheet:
  //   PC
  //   A
  //   B
  //   MAR
  //   MEMORY
  //   NAME: NISHANT ROY
  //   GTID: 903054614
  //   PRISM ID: nroy6
  //   IR
endmodule

module Micro_sequencer (
  input  [3:0] in_1,
  input  [1:0] in_2,
  output [4:0] out_3,
  output [5:0] out_4,
  output [1:0] out_5,
  output [1:0] out_6,
  output [1:0] out_7
);

  wire button_1_out, ChkCC, CLOCK_out, OPTest;
  wire [5:0] multiplexer_1_out, NextState, register_1_q, rom_2_data, rom_3_data;
  wire [31:25] rom_1_data;

  ROM #(.addrWidth(6), .dataWidth(32)) rom_1 (
    .addr(register_1_q), .data({rom_1_data, ChkCC, OPTest, out_7, out_6, out_5, out_4, out_3, NextState}));  // open: sel
  ROM #(.addrWidth(4), .dataWidth(6)) rom_2 (.addr(in_1), .data(rom_2_data));  // open: sel
  ROM #(.addrWidth(2), .dataWidth(6)) rom_3 (.addr(in_2), .data(rom_3_data));  // open: sel
  Multiplexer #(.select(2), .width(6), .disabled(0), .enable("false")) multiplexer_1 (
    .in0(NextState), .in1(rom_2_data), .in2(rom_3_data), .out(multiplexer_1_out), .sel({ChkCC, OPTest}));  // open: in3
  Register #(.width(6)) register_1 (
    .D(multiplexer_1_out), .Q(register_1_q), .clk(CLOCK_out), .clr(button_1_out));  // open: en
  Clock CLOCK (.out(CLOCK_out));
  Button button_1 (.out(button_1_out));

  // Other names for the same wires on the sheet: Drive[4:0] = out_3; Load[5:0] = out_4; Write[1:0] = out_5;
  //   RegSel[1:0] = out_6; ALU[1:0] = out_7

  // Notes on the sheet:
  //   Main ROM
  //   IR[31:28]
  //   CCMatch
  //   contents of rom_1 (hex, n*v repeats v):
  //   6201 1082 c00900 84044 108045 30100 84047 8408 30100 8404a 10804b 230100 100000d 420e 840f 900 20211
  //   80840 84053 8414 2115 30080 4217 8418 30100 8405a 841b 211c 40040 8405d 841e 630100 20
  //   contents of rom_2 (hex, n*v repeats v):
  //   3 6 9 c 10 12 16 19 1d 20
  //   contents of rom_3 (hex, n*v repeats v):
  //   0 d
endmodule

module ALU (
  input  [31:0] in_1,
  input  [31:0] in_2,
  input  [1:0] in_3,
  output [31:0] \output 
);

  wire [4:0] immVal;
  wire [31:0] adder_1_out, adder_2_out, multiplexer_1_out, nand_1_out, shifter_1_out, shifter_2_out,
       shifter_3_out;

  Adder #(.width(32)) adder_1 (.a(in_1), .b(in_2), .out(adder_1_out));  // open: cin, cout
  assign nand_1_out = ~(in_1 & in_2);  // NAND_Gate nand_1, 32 bits wide
  Adder #(.width(32)) adder_2 (.a(in_1), .b(32'h1), .out(adder_2_out));  // open: cin, cout
  Shifter #(.width(32)) shifter_1 (.in(in_1), .\dist (immVal), .out(shifter_1_out));
  Shifter #(.width(32), .shift("lr")) shifter_2 (.in(in_1), .\dist (immVal), .out(shifter_2_out));
  Shifter #(.width(32), .shift("ar")) shifter_3 (.in(in_1), .\dist (immVal), .out(shifter_3_out));
  Bit_Extender #(.in_width(32), .out_width(5), .\type ("sign")) bit_extender_1 (.in(in_2), .out(immVal));
  Multiplexer #(.select(2), .width(32), .disabled(0), .enable("false")) multiplexer_1 (
    .in0(shifter_1_out), .in1(shifter_2_out), .in2(shifter_1_out), .in3(shifter_3_out),
    .out(multiplexer_1_out), .sel(in_2[19:18]));
  Multiplexer #(.select(2), .width(32), .disabled(0), .enable("false")) multiplexer_2 (
    .in0(adder_1_out), .in1(nand_1_out), .in2(adder_2_out), .in3(multiplexer_1_out), .out(\output ),
    .sel(in_3));

  // Other names for the same wires on the sheet: A[31:0] = in_1; B[31:0] = in_2; ShiftD = in_2[18]; ShiftA = in_2[19]
endmodule

module regFile (
  input  in_1,
  input  [31:0] in_2,
  input  in_3,
  input  in_4,
  input  [3:0] in_5,
  output [31:0] out_6
);

  wire and_1_out, and_2_out, and_3_out, and_4_out, and_5_out, and_6_out, and_7_out, and_8_out, and_9_out,
       and_10_out, and_11_out, and_12_out, and_13_out, and_14_out, and_15_out, decoder_1_out1,
       decoder_1_out2, decoder_1_out3, decoder_1_out4, decoder_1_out5, decoder_1_out6, decoder_1_out7,
       decoder_1_out8, decoder_1_out9, decoder_1_out10, decoder_1_out11, decoder_1_out12, decoder_1_out13,
       decoder_1_out14, decoder_1_out15;
  wire [31:0] a0, a1, a2, at, fp, k0, ra, s0, s1, s2, sp, t0, t1, t2, v0;

  Decoder #(.select(4), .enable("false")) decoder_1 (
    .out1(decoder_1_out1), .out2(decoder_1_out2), .out3(decoder_1_out3), .out4(decoder_1_out4),
    .out5(decoder_1_out5), .out6(decoder_1_out6), .out7(decoder_1_out7), .out8(decoder_1_out8),
    .out9(decoder_1_out9), .out10(decoder_1_out10), .out11(decoder_1_out11), .out12(decoder_1_out12),
    .out13(decoder_1_out13), .out14(decoder_1_out14), .out15(decoder_1_out15), .sel(in_5));  // open: out0
  and and_1 (and_1_out, decoder_1_out1, in_3);
  and and_2 (and_2_out, decoder_1_out2, in_3);
  and and_3 (and_3_out, decoder_1_out3, in_3);
  and and_4 (and_4_out, decoder_1_out4, in_3);
  and and_5 (and_5_out, decoder_1_out5, in_3);
  and and_6 (and_6_out, decoder_1_out6, in_3);
  and and_7 (and_7_out, decoder_1_out7, in_3);
  and and_8 (and_8_out, decoder_1_out8, in_3);
  and and_9 (and_9_out, decoder_1_out9, in_3);
  and and_10 (and_10_out, decoder_1_out10, in_3);
  and and_11 (and_11_out, decoder_1_out11, in_3);
  and and_12 (and_12_out, decoder_1_out12, in_3);
  and and_13 (and_13_out, decoder_1_out13, in_3);
  and and_14 (and_14_out, decoder_1_out14, in_3);
  and and_15 (and_15_out, decoder_1_out15, in_3);
  Register #(.width(32)) register_1 (.D(in_2), .en(and_1_out), .Q(at), .clk(in_1), .clr(in_4));
  Register #(.width(32)) register_2 (.D(in_2), .en(and_2_out), .Q(v0), .clk(in_1), .clr(in_4));
  Register #(.width(32)) register_3 (.D(in_2), .en(and_3_out), .Q(a0), .clk(in_1), .clr(in_4));
  Register #(.width(32)) register_4 (.D(in_2), .en(and_4_out), .Q(a1), .clk(in_1), .clr(in_4));
  Register #(.width(32)) register_5 (.D(in_2), .en(and_5_out), .Q(a2), .clk(in_1), .clr(in_4));
  Register #(.width(32)) register_6 (.D(in_2), .en(and_6_out), .Q(t0), .clk(in_1), .clr(in_4));
  Register #(.width(32)) register_7 (.D(in_2), .en(and_7_out), .Q(t1), .clk(in_1), .clr(in_4));
  Register #(.width(32)) register_8 (.D(in_2), .en(and_8_out), .Q(t2), .clk(in_1), .clr(in_4));
  Register #(.width(32)) register_9 (.D(in_2), .en(and_9_out), .Q(s0), .clk(in_1), .clr(in_4));
  Register #(.width(32)) register_10 (.D(in_2), .en(and_10_out), .Q(s1), .clk(in_1), .clr(in_4));
  Register #(.width(32)) register_11 (.D(in_2), .en(and_11_out), .Q(s2), .clk(in_1), .clr(in_4));
  Register #(.width(32)) register_12 (.D(in_2), .en(and_12_out), .Q(k0), .clk(in_1), .clr(in_4));
  Register #(.width(32)) register_13 (.D(in_2), .en(and_13_out), .Q(sp), .clk(in_1), .clr(in_4));
  Register #(.width(32)) register_14 (.D(in_2), .en(and_14_out), .Q(fp), .clk(in_1), .clr(in_4));
  Register #(.width(32)) register_15 (.D(in_2), .en(and_15_out), .Q(ra), .clk(in_1), .clr(in_4));
  Multiplexer #(.select(4), .width(32), .disabled(0), .enable("false")) multiplexer_1 (
    .in0({32{1'b0}}), .in1(at), .in2(v0), .in3(a0), .in4(a1), .in5(a2), .in6(t0), .in7(t1), .in8(t2),
    .in9(s0), .in10(s1), .in11(s2), .in12(k0), .in13(sp), .in14(fp), .in15(ra), .out(out_6), .sel(in_5));

  // Other names for the same wires on the sheet: Clear = in_4; Clock = in_1; RegS[3:0] = in_5; RegVal[31:0] = in_2;
  //   WrReg = in_3
endmodule

module checkCC (
  input  [2:0] in_1,
  input  [2:0] in_2,
  output [1:0] out_3
);

  wire and_1_out, and_2_out, and_3_out, or_1_out;

  and and_1 (and_1_out, in_1[0], in_2[0]);
  and and_2 (and_2_out, in_1[1], in_2[1]);
  and and_3 (and_3_out, in_1[2], in_2[2]);
  or or_1 (or_1_out, and_1_out, and_2_out, and_3_out);
  assign out_3 = {{1{1'b0}}, or_1_out};  // Bit_Extender bit_extender_1

  // Other names for the same wires on the sheet: currCC[2:0] = in_1; NZP[2:0] = in_2
endmodule
