// Logisim project Roy_Nishant.circ as structural Verilog: 7 circuits, main circuit main
module main (
);

  wire Br_PC, Clear, CLK, JALR_PC, No_OP, undriven_2, WrEN;
  wire [3:0] multiplexer_11_out, multiplexer_12_out, multiplexer_15_out, OP_EX, OP_IF_IDRR, OP_MEM, OP_WB,
       RegSel, RX_EX, RX_IF_IDRR, RX_MEM, RX_RZ, RX_WB, RY_EX, RY_IF_IDRR, RY_MEM, RY_WB, RZ_IF_IDRR;
  wire [19:0] multiplexer_3_out, multiplexer_8_out, OFF_EX, OFF_IF_IDRR, OFF_MEM;
  wire [31:0] ALU, ALU_MEM, ALU_WB, bit_extender_1_out, bit_extender_2_out, BRANCH, Instruction,
       multiplexer_1_out, multiplexer_2_out, multiplexer_7_out, multiplexer_9_out, multiplexer_10_out,
       multiplexer_13_out, multiplexer_14_out, multiplexer_16_out, multiplexer_17_out, Out1, OUT1_EX,
       OUT1_MEM, Out2, OUT2_EX, OUT2_MEM, PC, PC_1_EX, PC_1_IF_IDRR, PC_1_MEM, PC_1_WB, PC___1, undriven,
       Updated_1, Updated_2, WR_Val;

  Clock CLOCK (.out(CLK));
  Button button_1 (.out(Clear));
  Multiplexer #(.width(32), .enable("false")) multiplexer_1 (
    .in0(OUT2_EX), .in1({32{1'b0}}), .out(multiplexer_1_out));  // open: sel
  ROM #(.addrWidth(24), .dataWidth(32)) rom_1 (.addr(PC[23:0]), .data(Instruction));  // open: sel
  Multiplexer #(.select(2), .width(32), .enable("false")) multiplexer_2 (
    .in0(PC___1), .in1(BRANCH), .in2(multiplexer_1_out), .in3(undriven), .out(multiplexer_2_out),
    .sel({Br_PC, JALR_PC}));
  IF_IDRR_Buffer if_idrr_buffer_1 (
    .in_2(Instruction), .in_3(PC___1), .in_4(CLK), .out_5(RZ_IF_IDRR), .out_6(RX_IF_IDRR),
    .out_7(OFF_IF_IDRR), .out_9(RY_IF_IDRR), .out_10(OP_IF_IDRR), .out_8(PC_1_IF_IDRR));  // open: in_1
  Adder #(.width(32)) adder_1 (.a(PC), .b(32'h1), .out(PC___1));  // open: cin, cout
  Register #(.width(32)) register_1 (.D(multiplexer_2_out), .Q(PC), .clk(CLK), .clr(Clear));  // open: en
  assign bit_extender_1_out = {{12{1'b0}}, multiplexer_3_out};  // Bit_Extender bit_extender_1
  Multiplexer #(.width(20), .enable("false")) multiplexer_3 (
    .in0(OFF_EX), .in1({20{1'b0}}), .out(multiplexer_3_out));  // open: sel
  Multiplexer #(.width(4), .enable("false")) multiplexer_4 (
    .in0(RX_IF_IDRR), .in1(RZ_IF_IDRR), .out(RX_RZ), .sel(undriven_2));
  Multiplexer #(.width(32), .enable("false")) multiplexer_5 (.in0(Out1), .in1(Updated_1));  // open: out, sel
  Multiplexer #(.width(32), .enable("false")) multiplexer_6 (.in0(Out2), .in1(Updated_2));  // open: out, sel
  Adder #(.width(32)) adder_2 (.a(PC___1), .b(bit_extender_1_out), .out(BRANCH));  // open: cin, cout
  Dual_Ported_Register_File dual_ported_register_file_1 (
    .CLK(CLK), .WrREGNO(RegSel), .RdREGNO1(RY_IF_IDRR), .RdREGNO2(RX_RZ), .INPUT(WR_Val), .OUT1(Out1),
    .OUT2(Out2), .WrEN(WrEN));
  Multiplexer #(.width(32), .enable("false")) multiplexer_7 (
    .in0(OUT2_EX), .in1({32{1'b0}}), .out(multiplexer_7_out), .sel(No_OP));
  Multiplexer #(.width(20), .enable("false")) multiplexer_8 (
    .in0(OFF_EX), .in1({20{1'b0}}), .out(multiplexer_8_out), .sel(No_OP));
  assign bit_extender_2_out = {{12{1'b0}}, multiplexer_8_out};  // Bit_Extender bit_extender_2
  Multiplexer #(.width(32), .enable("false")) multiplexer_9 (
    .in0(OUT1_EX), .in1({32{1'b0}}), .out(multiplexer_9_out), .sel(No_OP));
  Multiplexer #(.width(32), .enable("false")) multiplexer_10 (
    .in0(multiplexer_7_out), .in1(bit_extender_2_out), .out(multiplexer_10_out));  // open: sel
  IDRR_EX_Buffer idrr_ex_buffer_1 (
    .in_1(CLK), .in_2(OP_IF_IDRR), .in_3(RX_IF_IDRR), .in_4(RY_IF_IDRR), .in_5(OFF_IF_IDRR),
    .in_6(PC_1_IF_IDRR), .out_7(PC_1_EX), .out_8(OFF_EX), .out_9(RX_EX), .out_10(RY_EX), .out_12(OUT1_EX),
    .out_13(OUT2_EX), .out_11(OP_EX));
  ALU alu_1 (.in_1(multiplexer_9_out), .in_2(multiplexer_10_out), .\output (ALU));  // open: in_3
  Multiplexer #(.width(4), .enable("false")) multiplexer_11 (
    .in0(RY_EX), .in1(4'b0000), .out(multiplexer_11_out), .sel(No_OP));
  Multiplexer #(.width(4), .enable("false")) multiplexer_12 (
    .in0(OP_EX), .in1(4'b0000), .out(multiplexer_12_out), .sel(No_OP));
  Multiplexer #(.width(32), .enable("false")) multiplexer_13 (
    .in0(PC_1_EX), .in1({32{1'b0}}), .out(multiplexer_13_out), .sel(No_OP));
  Multiplexer #(.width(32), .enable("false")) multiplexer_14 (
    .in0(OUT2_EX), .in1({32{1'b0}}), .out(multiplexer_14_out), .sel(No_OP));
  Multiplexer #(.width(4), .enable("false")) multiplexer_15 (
    .in0(RX_EX), .in1(4'b0000), .out(multiplexer_15_out), .sel(No_OP));
  Multiplexer #(.width(32), .enable("false")) multiplexer_16 (
    .in0(ALU), .in1({32{1'b0}}), .out(multiplexer_16_out), .sel(No_OP));
  Multiplexer #(.width(32), .enable("false")) multiplexer_17 (
    .in0(OUT1_EX), .in1({32{1'b0}}), .out(multiplexer_17_out), .sel(No_OP));
  EX_MEM_Buffer ex_mem_buffer_1 (
    .in_1(CLK), .in_2(multiplexer_15_out), .in_3(multiplexer_11_out), .in_4(multiplexer_12_out),
    .in_5(multiplexer_13_out), .in_6(multiplexer_16_out), .in_7(multiplexer_17_out),
    .in_8(multiplexer_14_out), .out_9(PC_1_MEM), .out_10(OFF_MEM), .out_11(OP_MEM), .out_12(RX_MEM),
    .out_13(RY_MEM), .out_14(ALU_MEM), .out_15(OUT1_MEM), .out_16(OUT2_MEM));
  MEM_WB_Buffer mem_wb_buffer_1 (
    .in_1(CLK), .in_2(RX_MEM), .in_3(RY_MEM), .in_4(OP_MEM), .in_5(ALU_MEM), .in_6(PC_1_MEM), .out_7(RX_WB),
    .out_8(RY_WB), .out_9(OP_WB), .out_10(ALU_WB), .out_11(PC_1_WB));
endmodule

module Dual_Ported_Register_File (
  input  CLK,
  input  WrEN,
  input  [3:0] WrREGNO,
  input  [3:0] RdREGNO1,
  input  [3:0] RdREGNO2,
  input  [31:0] INPUT,
  output [31:0] OUT1,
  output [31:0] OUT2
);

  wire En_a0, En_a1, En_a2, En_at, En_fp, En_k0, En_ra, En_s0, En_s1, En_s2, En_sp, En_t0, En_t1, En_t2,
       En_v0;
  wire [31:0] a0, a1, a2, at, fp, k0, ra, s0, s1, s2, sp, t0, t1, t2, v0, zero;

  Decoder #(.select(4), .disabled(0)) decoder_1 (
    .out1(En_at), .out2(En_v0), .out3(En_a0), .out4(En_a1), .out5(En_a2), .out6(En_t0), .out7(En_t1),
    .out8(En_t2), .out9(En_s0), .out10(En_s1), .out11(En_s2), .out12(En_k0), .out13(En_sp), .out14(En_fp),
    .out15(En_ra), .sel(WrREGNO), .en(WrEN));  // open: out0
  Register #(.width(32)) u_zero (.D(INPUT), .en(1'b0), .Q(zero), .clk(CLK));  // open: clr
  Register #(.width(32)) u_at (.D(INPUT), .en(En_at), .Q(at), .clk(CLK));  // open: clr
  Register #(.width(32)) u_v0 (.D(INPUT), .en(En_v0), .Q(v0), .clk(CLK));  // open: clr
  Register #(.width(32)) u_a0 (.D(INPUT), .en(En_a0), .Q(a0), .clk(CLK));  // open: clr
  Register #(.width(32)) u_a1 (.D(INPUT), .en(En_a1), .Q(a1), .clk(CLK));  // open: clr
  Register #(.width(32)) u_a2 (.D(INPUT), .en(En_a2), .Q(a2), .clk(CLK));  // open: clr
  Register #(.width(32)) u_t0 (.D(INPUT), .en(En_t0), .Q(t0), .clk(CLK));  // open: clr
  Register #(.width(32)) u_t1 (.D(INPUT), .en(En_t1), .Q(t1), .clk(CLK));  // open: clr
  Multiplexer #(.select(4), .width(32), .disabled(0), .enable("false")) multiplexer_1 (
    .in0(zero), .in1(at), .in2(v0), .in3(a0), .in4(a1), .in5(a2), .in6(t0), .in7(t1), .in8(t2), .in9(s0),
    .in10(s1), .in11(s2), .in12(k0), .in13(sp), .in14(fp), .in15(ra), .out(OUT2), .sel(RdREGNO2));
  Register #(.width(32)) u_t2 (.D(INPUT), .en(En_t2), .Q(t2), .clk(CLK));  // open: clr
  Register #(.width(32)) u_s0 (.D(INPUT), .en(En_s0), .Q(s0), .clk(CLK));  // open: clr
  Register #(.width(32)) u_s1 (.D(INPUT), .en(En_s1), .Q(s1), .clk(CLK));  // open: clr
  Register #(.width(32)) u_s2 (.D(INPUT), .en(En_s2), .Q(s2), .clk(CLK));  // open: clr
  Register #(.width(32)) u_k0 (.D(INPUT), .en(En_k0), .Q(k0), .clk(CLK));  // open: clr
  Register #(.width(32)) u_sp (.D(INPUT), .en(En_sp), .Q(sp), .clk(CLK));  // open: clr
  Register #(.width(32)) u_fp (.D(INPUT), .en(En_fp), .Q(fp), .clk(CLK));  // open: clr
  Register #(.width(32)) u_ra (.D(INPUT), .en(En_ra), .Q(ra), .clk(CLK));  // open: clr
  Multiplexer #(.select(4), .width(32), .disabled(0), .enable("false")) multiplexer_2 (
    .in0(zero), .in1(at), .in2(v0), .in3(a0), .in4(a1), .in5(a2), .in6(t0), .in7(t1), .in8(t2), .in9(s0),
    .in10(s1), .in11(s2), .in12(k0), .in13(sp), .in14(fp), .in15(ra), .out(OUT1), .sel(RdREGNO1));

  // Notes on the sheet:
  //   MODIFY AT YOUR OWN RISK
endmodule

module IF_IDRR_Buffer (
  input  in_1,
  input  [31:0] in_2,
  input  [31:0] in_3,
  input  in_4,
  output [3:0] out_5,
  output [3:0] out_6,
  output [19:0] out_7,
  output [31:0] out_8,
  output [3:0] out_9,
  output [3:0] out_10
);

  wire [31:0] multiplexer_1_out, multiplexer_2_out;

  Multiplexer #(.width(32), .enable("false")) multiplexer_1 (
    .in0(in_2), .in1({32{1'b0}}), .out(multiplexer_1_out), .sel(in_1));
  Multiplexer #(.width(32), .enable("false")) multiplexer_2 (
    .in0(in_3), .in1({32{1'b0}}), .out(multiplexer_2_out), .sel(in_1));
  Register #(.width(32)) register_1 (
    .D(multiplexer_1_out), .Q({out_10, out_6, out_9, out_7[19:4], out_5}), .clk(in_4));  // open: en, clr
  Register #(.width(32)) register_2 (.D(multiplexer_2_out), .Q(out_8), .clk(in_4));  // open: en, clr

  assign out_7[3:0] = out_5;

  // Other names for the same wires on the sheet: Offset[19:0] = {out_7[19:4], out_5}; RZ[3:0] = out_5;
  //   RY[3:0] = out_9; RX[3:0] = out_6; OP[3:0] = out_10; Clock = in_4; Flush = in_1; Instruction[31:0] = in_2;
  //   PC___1[31:0] = in_3; PC___1_OUT[31:0] = out_8
endmodule

module IDRR_EX_Buffer (
  input  in_1,
  input  [3:0] in_2,
  input  [3:0] in_3,
  input  [3:0] in_4,
  input  [19:0] in_5,
  input  [31:0] in_6,
  output [31:0] out_7,
  output [19:0] out_8,
  output [3:0] out_9,
  output [3:0] out_10,
  output [3:0] out_11,
  output [31:0] out_12,
  output [31:0] out_13
);


  // Other names for the same wires on the sheet: CLK = in_1; OFF_EX[19:0] = out_8; OFF_IDRR[19:0] = in_5;
  //   OP_EX[3:0] = out_11; OP_IDRR[3:0] = in_2; OUT_1_EX[31:0] = out_12; OUT_2_EX[31:0] = out_13;
  //   PC___1_EX[31:0] = out_7; PC___1_IDRR[31:0] = in_6; RX_EX[3:0] = out_9; RX_IDRR[3:0] = in_3; RY_EX[3:0] = out_10;
  //   RY_IDRR[3:0] = in_4
endmodule

module EX_MEM_Buffer (
  input  in_1,
  input  [3:0] in_2,
  input  [3:0] in_3,
  input  [3:0] in_4,
  input  [31:0] in_5,
  input  [31:0] in_6,
  input  [31:0] in_7,
  input  [31:0] in_8,
  output [31:0] out_9,
  output [19:0] out_10,
  output [3:0] out_11,
  output [3:0] out_12,
  output [3:0] out_13,
  output [31:0] out_14,
  output [31:0] out_15,
  output [31:0] out_16
);


  // Other names for the same wires on the sheet: ALU_EX[31:0] = in_6; ALU_MEM[31:0] = out_14; CLK = in_1;
  //   OFF_MEM[19:0] = out_10; OP_EX[3:0] = in_4; OP_MEM[3:0] = out_11; OUT_1_EX[31:0] = in_7;
  //   OUT_1_MEM[31:0] = out_15; OUT_2_EX[31:0] = in_8; OUT_2_MEM[31:0] = out_16; PC___1_EX[31:0] = in_5;
  //   PC___1_MEM[31:0] = out_9; RX_EX[3:0] = in_2; RX_MEM[3:0] = out_12; RY_EX[3:0] = in_3; RY_MEM[3:0] = out_13
endmodule

module MEM_WB_Buffer (
  input  in_1,
  input  [3:0] in_2,
  input  [3:0] in_3,
  input  [3:0] in_4,
  input  [31:0] in_5,
  input  [31:0] in_6,
  output [3:0] out_7,
  output [3:0] out_8,
  output [3:0] out_9,
  output [31:0] out_10,
  output [31:0] out_11
);


  // Other names for the same wires on the sheet: ALU_MEM[31:0] = in_5; ALU_WB[31:0] = out_10; CLK = in_1;
  //   OP_MEM[3:0] = in_4; OP_WB[3:0] = out_9; PC_1_MEM[31:0] = in_6; PC_1_WB[31:0] = out_11; RX_MEM[3:0] = in_2;
  //   RX_WB[3:0] = out_7; RY_MEM[3:0] = in_3; RY_WB[3:0] = out_8
endmodule

module ALU (
  input  [31:0] in_1,
  input  [31:0] in_2,
  input  [1:0] in_3,
  output [31:0] \output 
);

  wire [4:0] immVal;
  wire [31:0] adder_1_out, adder_2_out, multiplexer_1_out, nand_1_out, shifter_1_out, shifter_2_out,
       shifter_3_out;

  Adder #(.width(32)) adder_1 (.a(in_1), .b(in_2), .out(adder_1_out));  // open: cin, cout
  assign nand_1_out = ~(in_1 & in_2);  // NAND_Gate nand_1, 32 bits wide
  Adder #(.width(32)) adder_2 (.a(in_1), .b(32'h1), .out(adder_2_out));  // open: cin, cout
  Shifter #(.width(32)) shifter_1 (.in(in_1), .\dist (immVal), .out(shifter_1_out));
  Shifter #(.width(32), .shift("lr")) shifter_2 (.in(in_1), .\dist (immVal), .out(shifter_2_out));
  Shifter #(.width(32), .shift("ar")) shifter_3 (.in(in_1), .\dist (immVal), .out(shifter_3_out));
  Bit_Extender #(.in_width(32), .out_width(5), .\type ("sign")) bit_extender_1 (.in(in_2), .out(immVal));
  Multiplexer #(.select(2), .width(32), .disabled(0), .enable("false")) multiplexer_1 (
    .in0(shifter_1_out), .in1(shifter_2_out), .in2(shifter_1_out), .in3(shifter_3_out),
    .out(multiplexer_1_out), .sel(in_2[19:18]));
  Multiplexer #(.select(2), .width(32), .disabled(0), .enable("false")) multiplexer_2 (
    .in0(adder_1_out), .in1(nand_1_out), .in2(adder_2_out), .in3(multiplexer_1_out), .out(\output ),
    .sel(in_3));

  // Other names for the same wires on the sheet: A[31:0] = in_1; B[31:0] = in_2; ShiftD = in_2[18]; ShiftA = in_2[19]
endmodule
